# Fritzing sketch intel_hck_carnsics (saved by Fritzing 0.9.3b)

parts:
  Part1 = Arduino 101
  Part2 = Arduino Uno (Rev3)
  Part3 = MicroSD Card Module
  ZS-042_RTC1 = ZS-042 RTC Module
  Part4 = LCD1602-I2C
  Grove1 = Grove Button
  U2 = SUP500F [package=sup500f]
  Grove2 = Grove Buzz

nets:
  N1: Part1.A1, ZS-042_RTC1.VCC
  N2: Part1.A4/SDA, ZS-042_RTC1.SDA, Part4.SDA
  N3: Part1.A5/SCL, ZS-042_RTC1.SCL, Part4.SCL
  N4: Part1.D8, Grove1.SIG
  N5: Part1.D10_PWM/SS, Part3.CS
  N6: Part1.D11_PWM/MOSI, Part3.MOSI
  N7: Part1.D12/MISO, Part3.MISO
  N8: Part1.D13/SCK, Part3.SCK
  N9: Part1.D4, Part2.D0/RX
  N10: Part1.D5_PWM, Part2.D1/TX
  N11: Part1.D6_PWM, Grove2.SIG
  3V3: Part1.3V3, Part3.VCC
  5V: Part1.5V, Part4.VCC
  GND: Part1.GND, ZS-042_RTC1.GND
  N12: Part2.D3_PWM, U2.TX-O
  N13: Part2.D4, U2.RX-I
  5V_2: Part2.5V, U2.VCC
  GND_2: Part2.GND, U2.GND

custom parts:
  Arduino 101: A learning and development board that delivers the performance and low-power consumption of the Intel® Curie™ Module with the simplicity of Arduino at an entry-level price. It keeps the same robust form factor and peripheral list of the UNO with the addition of onboard Bluetooth LE capabilities and a 6-axis accelerometer/gyro to help you easily expand your creativity into the connected world.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
  LCD1602-I2C: A standard character display, usually with 2x16 characters. Comes in many colors with LCM1602 IIC attached.
